# Fritzing sketch schematic (saved by Fritzing 0.9.2b)
breadboards: 1

parts:
  Part1 = Arduino Uno (Rev3)
  J1 = Piezo Speaker
  R1 = PHOTOCELL [package=photocell-kit]

nets:
  N1: Part1.A0, R1.P$1
  N2: Part1.D8, J1.pin2
  N3: Part1.GND, J1.pin1
  N4: Part1.5V, R1.P$2
