# Fritzing sketch schematic (saved by Fritzing 0.9.2b)
breadboards: 1

parts:
  Part1 = Arduino Uno (Rev3)
  R1 = Resistor [tolerance=±5% resistance=220 package=THT]
  R2 = Resistor [tolerance=±5% resistance=220 package=THT]
  R3 = Resistor [tolerance=±5% resistance=220 package=THT]
  LED1 = RGB LED (com. cathode, rbg) [package="5 mm [THT]"]
  R4 = PHOTOCELL [package=photocell-kit]
  R5 = PHOTOCELL [package=photocell-kit]
  R6 = PHOTOCELL [package=photocell-kit]
  R7 = Resistor [tolerance=±5% resistance=10k package=THT]
  R8 = Resistor [tolerance=±5% resistance=10k package=THT]  # not connected
  R9 = Resistor [tolerance=±5% resistance=10k package=THT]

nets:
  N1: Part1.A0, R4.P$1, R7.Pin_0
  N2: Part1.A1, R5.P$1
  N3: Part1.A2, R6.P$1, R9.Pin_0
  N4: Part1.D9_PWM, R3.Pin_0
  N5: Part1.D10_PWM/SS, R2.Pin_0
  N6: Part1.D11_PWM/MOSI, R1.Pin_0
  N7: Part1.GND, LED1.common_cathode
  N8: Part1.5V, R4.P$2, R5.P$2, R6.P$2, R7.Pin_1, R9.Pin_1
  N9: R1.Pin_1, LED1.red_anode
  N10: R2.Pin_1, LED1.blue_anode
  N11: R3.Pin_1, LED1.green_anode
